# Fritzing sketch AnalogInputOutput (saved by Fritzing 0.1.b)
breadboards: 1

parts:
  Arduino1 = Arduino Diecimila (deprecated) [package=THT]
  LED1 = Red LED - 5mm
  R1 = Trimmer Potentiometer [package=THT]
  R2 = basic-resistor-220

nets:
  N1: Arduino1.D3, R2.connector1
  N2: Arduino1.+5V, R1.leg1
  N3: Arduino1.GND, Arduino1.ground, LED1.cathode, R1.leg2
  N4: Arduino1.A2, R1.wiper
  N5: LED1.anode, R2.connector0
