# Fritzing sketch AnalogInputPot (saved by Fritzing 0.1.b)
breadboards: 3

parts:
  Arduino1 = Arduino Diecimila (deprecated) [package=THT]
  R1 = Trimmer Potentiometer [package=THT]
  LED1 = Red LED - 5mm

nets:
  N1: Arduino1.GND, R1.leg2, LED1.cathode
  N2: Arduino1.D13, LED1.anode
  N3: Arduino1.+5V, R1.leg1
  N4: Arduino1.A2, R1.wiper
