# Fritzing sketch Button (saved by Fritzing 0.1.b)
breadboards: 1

parts:
  Arduino1 = Arduino Diecimila (deprecated) [package=THT]
  S1 = Pushbutton [package=THT]
  R1 = basic-resistor-1k
  LED1 = Red LED - 5mm

nets:
  N1: Arduino1.GND, Arduino1.ground, R1.connector0, LED1.cathode
  N2: Arduino1.D13, LED1.anode
  N3: Arduino1.D2, S1.leg1, R1.connector1
  N4: Arduino1.+5V, S1.leg0
