# Fritzing sketch 555TouchSwitch (saved by Fritzing 0.3.4b)
breadboards: 1

parts:
  U1 = 555 Timer [package="DIP8 [THT]"]
  R1 = 100k Ω Resistor [package=THT]
  C2 = Ceramic Capacitor [package=THT]
  C5 = Electrolytic Capacitor [package=THT]
  Arduino2 = Arduino
  ANT1 = Antenna

nets:
  N1: U1.Ground, C2.pin_0, C5.-, Arduino2.GND
  N2: U1.Trigger, ANT1.antenna_lead
  N3: U1.Output, Arduino2.D6
  N4: U1.Reset, U1.Vcc_Supply_Voltage, R1.Pin_0, Arduino2.+5V
  N5: U1.Control_Voltage, C2.pin_1
  N6: U1.Threshold, U1.Discharge, R1.Pin_1, C5.+

notes:
  This is a 555 timer touch switch circuit based on a Forrest Mims circuit. The yellow wire serves as the touch sensor. Pin 3 on the 555 timer is the output signal and is read by Pin 6 on the Arduino.
  http://talkingelectronics.com/projects/TouchSwitch/TouchSwitch-1.html
